// Logisim project 16 x 16 Register.circ as structural Verilog: 2 circuits, main circuit 16 bit register
module _16_bit_register (
  input  [15:0] _16bit_input,
  input  clock,
  input  reset,
  output [15:0] out_4
);

  Register #(.width(1)) register_1 (.D(_16bit_input[0]), .Q(out_4[0]), .clk(clock), .clr(reset));  // open: en
  Register #(.width(1)) register_2 (.D(_16bit_input[1]), .Q(out_4[1]), .clk(clock), .clr(reset));  // open: en
  Register #(.width(1)) register_3 (.D(_16bit_input[2]), .Q(out_4[2]), .clk(clock), .clr(reset));  // open: en
  Register #(.width(1)) register_4 (.D(_16bit_input[3]), .Q(out_4[3]), .clk(clock), .clr(reset));  // open: en
  Register #(.width(1)) register_5 (.D(_16bit_input[4]), .Q(out_4[4]), .clk(clock), .clr(reset));  // open: en
  Register #(.width(1)) register_6 (.D(_16bit_input[5]), .en(_16bit_input[5]), .Q(out_4[5]), .clk(clock), .clr(reset));
  Register #(.width(1)) register_7 (.D(_16bit_input[6]), .Q(out_4[6]), .clk(clock), .clr(reset));  // open: en
  Register #(.width(1)) register_8 (.D(_16bit_input[7]), .Q(out_4[7]), .clk(clock), .clr(reset));  // open: en
  Register #(.width(1)) register_9 (.D(_16bit_input[8]), .Q(out_4[8]), .clk(clock), .clr(reset));  // open: en
  Register #(.width(1)) register_10 (.D(_16bit_input[9]), .Q(out_4[9]), .clk(clock), .clr(reset));  // open: en
  Register #(.width(1)) register_11 (.D(_16bit_input[10]), .Q(out_4[10]), .clk(clock), .clr(reset));  // open: en
  Register #(.width(1)) register_12 (.D(_16bit_input[11]), .Q(out_4[11]), .clk(clock), .clr(reset));  // open: en
  Register #(.width(1)) register_13 (.D(_16bit_input[12]), .Q(out_4[12]), .clk(clock), .clr(reset));  // open: en
  Register #(.width(1)) register_14 (.D(_16bit_input[13]), .Q(out_4[13]), .clk(clock), .clr(reset));  // open: en
  Register #(.width(1)) register_15 (.D(_16bit_input[14]), .Q(out_4[14]), .clk(clock), .clr(reset));  // open: en
  Register #(.width(1)) register_16 (.D(_16bit_input[15]), .Q(out_4[15]), .clk(clock), .clr(reset));  // open: en
endmodule

module _16_x_16 (
  input  [15:0] in_1,
  input  [15:0] in_2,
  input  [15:0] in_3,
  input  [15:0] in_4,
  input  [15:0] in_5,
  input  [15:0] in_6,
  input  [15:0] in_7,
  input  [15:0] in_8,
  input  [15:0] in_9,
  input  [15:0] in_10,
  input  [15:0] in_11,
  input  [15:0] in_12,
  input  [15:0] in_13,
  input  [15:0] in_14,
  input  [15:0] in_15,
  input  [15:0] in_16,
  input  clk,
  input  rst,
  input  [3:0] in_19,
  output [15:0] out_20,
  output [15:0] out_21,
  output [15:0] out_22,
  output [15:0] out_23,
  output [15:0] out_24,
  output [15:0] out_25,
  output [15:0] out_26,
  output [15:0] out_27,
  output [15:0] out_28,
  output [15:0] out_29,
  output [15:0] out_30,
  output [15:0] out_31,
  output [15:0] out_32,
  output [15:0] out_33,
  output [15:0] out_34,
  output [15:0] out_35
);

  wire demultiplexer_1_out0, demultiplexer_1_out1, demultiplexer_1_out2, demultiplexer_1_out3,
       demultiplexer_1_out4, demultiplexer_1_out5, demultiplexer_1_out6, demultiplexer_1_out7,
       demultiplexer_1_out8, demultiplexer_1_out9, demultiplexer_1_out10, demultiplexer_1_out11,
       demultiplexer_1_out12, demultiplexer_1_out13, demultiplexer_1_out14, demultiplexer_1_out15;

  Demultiplexer #(.select(4)) demultiplexer_1 (
    .out0(demultiplexer_1_out0), .out1(demultiplexer_1_out1), .out2(demultiplexer_1_out2),
    .out3(demultiplexer_1_out3), .out4(demultiplexer_1_out4), .out5(demultiplexer_1_out5),
    .out6(demultiplexer_1_out6), .out7(demultiplexer_1_out7), .out8(demultiplexer_1_out8),
    .out9(demultiplexer_1_out9), .out10(demultiplexer_1_out10), .out11(demultiplexer_1_out11),
    .out12(demultiplexer_1_out12), .out13(demultiplexer_1_out13), .out14(demultiplexer_1_out14),
    .out15(demultiplexer_1_out15), .in(clk), .sel(in_19));  // open: en
  _16_bit_register u_16_bit_register_1 (._16bit_input(in_1), .clock(demultiplexer_1_out0), .reset(rst), .out_4(out_20));
  _16_bit_register u_16_bit_register_2 (._16bit_input(in_2), .clock(demultiplexer_1_out1), .reset(rst), .out_4(out_21));
  _16_bit_register u_16_bit_register_3 (._16bit_input(in_3), .clock(demultiplexer_1_out2), .reset(rst), .out_4(out_22));
  _16_bit_register u_16_bit_register_4 (._16bit_input(in_4), .clock(demultiplexer_1_out3), .reset(rst), .out_4(out_23));
  _16_bit_register u_16_bit_register_5 (._16bit_input(in_5), .clock(demultiplexer_1_out4), .reset(rst), .out_4(out_24));
  _16_bit_register u_16_bit_register_6 (._16bit_input(in_6), .clock(demultiplexer_1_out5), .reset(rst), .out_4(out_25));
  _16_bit_register u_16_bit_register_7 (._16bit_input(in_7), .clock(demultiplexer_1_out6), .reset(rst), .out_4(out_26));
  _16_bit_register u_16_bit_register_8 (._16bit_input(in_8), .clock(demultiplexer_1_out7), .reset(rst), .out_4(out_27));
  _16_bit_register u_16_bit_register_9 (._16bit_input(in_9), .clock(demultiplexer_1_out8), .reset(rst), .out_4(out_28));
  _16_bit_register u_16_bit_register_10 (
    ._16bit_input(in_10), .clock(demultiplexer_1_out9), .reset(rst), .out_4(out_29));
  _16_bit_register u_16_bit_register_11 (
    ._16bit_input(in_11), .clock(demultiplexer_1_out10), .reset(rst), .out_4(out_30));
  _16_bit_register u_16_bit_register_12 (
    ._16bit_input(in_12), .clock(demultiplexer_1_out11), .reset(rst), .out_4(out_31));
  _16_bit_register u_16_bit_register_13 (
    ._16bit_input(in_13), .clock(demultiplexer_1_out12), .reset(rst), .out_4(out_32));
  _16_bit_register u_16_bit_register_14 (
    ._16bit_input(in_14), .clock(demultiplexer_1_out13), .reset(rst), .out_4(out_33));
  _16_bit_register u_16_bit_register_15 (
    ._16bit_input(in_15), .clock(demultiplexer_1_out14), .reset(rst), .out_4(out_34));
  _16_bit_register u_16_bit_register_16 (
    ._16bit_input(in_16), .clock(demultiplexer_1_out15), .reset(rst), .out_4(out_35));
endmodule
