// Logisim project snake.circ as structural Verilog: 1 circuit, main circuit main
module main (
  input  in_1
);

  wire _0, _1, _2, _3, _4, _5, _6, _7, _8, _9, _10, _11, _12, _13, _14, _15, clock_1_out, comparator_2_eq,
       comparator_3_eq, comparator_4_gt, E, L, not_1_out, or_1_out, or_4_out, RST, tunnel;
  wire [3:0] undriven_2;
  wire [7:0] adder_1_out, counter_2_q, counter_3_q, Head, Keyboard_out, multiplexer_1_out, multiplexer_2_out,
       Rank, rom_1_data, Score, subtractor_2_out, undriven;
  wire [7:4] Head_1;
  wire [15:0] demultiplexer_1_out0, demultiplexer_1_out1, demultiplexer_1_out2, demultiplexer_1_out3,
       demultiplexer_1_out4, demultiplexer_1_out5, demultiplexer_1_out6, demultiplexer_1_out7,
       demultiplexer_1_out8, demultiplexer_1_out9, demultiplexer_1_out10, demultiplexer_1_out11,
       demultiplexer_1_out12, demultiplexer_1_out13, demultiplexer_1_out14, demultiplexer_1_out15,
       Display_line, n16_x_16_1_out_20, n16_x_16_1_out_21, n16_x_16_1_out_22, n16_x_16_1_out_23,
       n16_x_16_1_out_24, n16_x_16_1_out_25, n16_x_16_1_out_26, n16_x_16_1_out_27, n16_x_16_1_out_28,
       n16_x_16_1_out_29, n16_x_16_1_out_30, n16_x_16_1_out_31, n16_x_16_1_out_32, n16_x_16_1_out_33,
       n16_x_16_1_out_34, n16_x_16_1_out_35, n16_x_16_2_out_20, n16_x_16_2_out_21, n16_x_16_2_out_22,
       n16_x_16_2_out_23, n16_x_16_2_out_24, n16_x_16_2_out_25, n16_x_16_2_out_26, n16_x_16_2_out_27,
       n16_x_16_2_out_28, n16_x_16_2_out_29, n16_x_16_2_out_30, n16_x_16_2_out_31, n16_x_16_2_out_32,
       n16_x_16_2_out_33, n16_x_16_2_out_34, n16_x_16_2_out_35;

  or or_1 (or_1_out, RST, _8);
  Counter counter_1 (.Q(Score), .clk(tunnel), .clr(RST));  // open: load, D, count, carry
  Counter counter_2 (.Q(counter_2_q), .clk(comparator_3_eq), .clr(or_1_out));  // open: load, D, count, carry
  Clock clock_1 (.out(clock_1_out));
  Comparator comparator_1 (.a(Keyboard_out), .b(8'h61));  // open: gt, eq, lt
  Comparator comparator_2 (.a(Keyboard_out), .b(8'h64), .eq(comparator_2_eq));  // open: gt, lt
  Adder adder_1 (.a(Score), .b(8'h2), .out(adder_1_out));  // open: cin, cout
  // OR_Gate or_2 has open pins: in0=tunnel, in1=E, out=open
  ROM rom_1 (.addr(counter_2_q), .data(rom_1_data));  // open: sel
  or or_3 (RST, in_1, L);
  Multiplexer #(.width(8)) multiplexer_1 (
    .in0(Rank), .in1({Head_1, Head[3:0]}), .out(multiplexer_1_out), .sel(_0));  // open: en
  Multiplexer #(.width(8)) multiplexer_2 (
    .in0(subtractor_2_out), .in1(adder_1_out), .out(multiplexer_2_out), .sel(_0));  // open: en
  not not_1 (not_1_out, comparator_3_eq);
  Counter counter_3 (
    .load(comparator_3_eq), .D(rom_1_data), .count(not_1_out), .Q(counter_3_q), .clk(clock_1_out), .clr(RST));  // open: carry
  Comparator #(.width(16)) comparator_3 (
    .a({_15, _14, _13, _12, _11, _10, _9, _8, _7, _6, _5, _4, _3, _2, _1, _0}), .b({16{1'b0}}),
    .eq(comparator_3_eq));  // open: gt, lt
  ROM #(.dataWidth(16)) rom_2 (
    .addr(counter_3_q), .data({_15, _14, _13, _12, _11, _10, _9, _8, _7, _6, _5, _4, _3, _2, _1, _0}));  // open: sel
  Subtractor #(.width(4)) subtractor_1 (.a(Head[7:4]), .b(4'b0001), .out(Head_1));  // open: bin, bout
  Comparator comparator_4 (.a(undriven), .b({8{1'b0}}), .gt(comparator_4_gt));  // open: eq, lt
  Subtractor subtractor_2 (.a(undriven), .b({8{1'b0}}), .out(subtractor_2_out), .bin(comparator_4_gt));  // open: bout
  Demultiplexer #(.select(4), .width(16)) demultiplexer_1 (
    .out0(demultiplexer_1_out0), .out1(demultiplexer_1_out1), .out2(demultiplexer_1_out2),
    .out3(demultiplexer_1_out3), .out4(demultiplexer_1_out4), .out5(demultiplexer_1_out5),
    .out6(demultiplexer_1_out6), .out7(demultiplexer_1_out7), .out8(demultiplexer_1_out8),
    .out9(demultiplexer_1_out9), .out10(demultiplexer_1_out10), .out11(demultiplexer_1_out11),
    .out12(demultiplexer_1_out12), .out13(demultiplexer_1_out13), .out14(demultiplexer_1_out14),
    .out15(demultiplexer_1_out15), .in(Display_line), .sel(undriven_2));  // open: en
  or or_4 (or_4_out, _9, RST);
  _16_x_16 u_16_x_16_1 (
    .in_1(demultiplexer_1_out0), .in_2(demultiplexer_1_out1), .in_3(demultiplexer_1_out2),
    .in_4(demultiplexer_1_out3), .in_5(demultiplexer_1_out4), .in_6(demultiplexer_1_out5),
    .in_7(demultiplexer_1_out6), .in_8(demultiplexer_1_out7), .in_9(demultiplexer_1_out8),
    .in_10(demultiplexer_1_out9), .in_11(demultiplexer_1_out10), .in_12(demultiplexer_1_out11),
    .in_13(demultiplexer_1_out12), .in_14(demultiplexer_1_out13), .in_15(demultiplexer_1_out14),
    .in_16(demultiplexer_1_out15), .clk(_5), .rst(or_4_out), .in_19(undriven_2), .out_20(n16_x_16_1_out_20),
    .out_21(n16_x_16_1_out_21), .out_22(n16_x_16_1_out_22), .out_23(n16_x_16_1_out_23),
    .out_24(n16_x_16_1_out_24), .out_25(n16_x_16_1_out_25), .out_26(n16_x_16_1_out_26),
    .out_27(n16_x_16_1_out_27), .out_28(n16_x_16_1_out_28), .out_29(n16_x_16_1_out_29),
    .out_30(n16_x_16_1_out_30), .out_31(n16_x_16_1_out_31), .out_32(n16_x_16_1_out_32),
    .out_33(n16_x_16_1_out_33), .out_34(n16_x_16_1_out_34), .out_35(n16_x_16_1_out_35));
  _16_x_16 u_16_x_16_2 (
    .in_1(n16_x_16_1_out_20), .in_2(n16_x_16_1_out_21), .in_3(n16_x_16_1_out_22), .in_4(n16_x_16_1_out_23),
    .in_5(n16_x_16_1_out_24), .in_6(n16_x_16_1_out_25), .in_7(n16_x_16_1_out_26), .in_8(n16_x_16_1_out_27),
    .in_9(n16_x_16_1_out_28), .in_10(n16_x_16_1_out_29), .in_11(n16_x_16_1_out_30),
    .in_12(n16_x_16_1_out_31), .in_13(n16_x_16_1_out_32), .in_14(n16_x_16_1_out_33),
    .in_15(n16_x_16_1_out_34), .in_16(n16_x_16_1_out_35), .clk(_6), .rst(RST), .out_20(n16_x_16_2_out_20),
    .out_21(n16_x_16_2_out_21), .out_22(n16_x_16_2_out_22), .out_23(n16_x_16_2_out_23),
    .out_24(n16_x_16_2_out_24), .out_25(n16_x_16_2_out_25), .out_26(n16_x_16_2_out_26),
    .out_27(n16_x_16_2_out_27), .out_28(n16_x_16_2_out_28), .out_29(n16_x_16_2_out_29),
    .out_30(n16_x_16_2_out_30), .out_31(n16_x_16_2_out_31), .out_32(n16_x_16_2_out_32),
    .out_33(n16_x_16_2_out_33), .out_34(n16_x_16_2_out_34), .out_35(n16_x_16_2_out_35));  // open: in_19
  DotMatrix #(.inputtype("row"), .matrixcols(16), .matrixrows(16)) dotmatrix_1 (
    .row0(n16_x_16_2_out_20), .row1(n16_x_16_2_out_21), .row2(n16_x_16_2_out_22), .row3(n16_x_16_2_out_23),
    .row4(n16_x_16_2_out_24), .row5(n16_x_16_2_out_25), .row6(n16_x_16_2_out_26), .row7(n16_x_16_2_out_27),
    .row8(n16_x_16_2_out_28), .row9(n16_x_16_2_out_29), .row10(n16_x_16_2_out_30), .row11(n16_x_16_2_out_31),
    .row12(n16_x_16_2_out_32), .row13(n16_x_16_2_out_33), .row14(n16_x_16_2_out_34), .row15(n16_x_16_2_out_35));

  // Other names for the same wires on the sheet: Head_1[3:0] = Head[3:0]
endmodule
